// Logisim project sqrt2.circ as structural Verilog: 35 circuits, main circuit main
module main (
  input  ENABLE,
  input  [15:0] IO_DATA_IN,
  output NAN,
  output PINF,
  output NINF,
  output RESULT,
  output [15:0] IO_DATA_OUT
);

  wire CLK_out;

  Clock CLK (.out(CLK_out));
  sqrt sqrt_1 (
    .CLK(CLK_out), .ENABLE(ENABLE), .IO_DATA_IN(IO_DATA_IN), .IS_NAN(NAN), .IS_PINF(PINF), .IS_NINF(NINF),
    .RESULT(RESULT), .IO_DATA_OUT(IO_DATA_OUT));
endmodule

module sqrt (
  input  CLK,
  input  ENABLE,
  input  [15:0] IO_DATA_IN,
  output IS_NAN,
  output IS_PINF,
  output IS_NINF,
  output RESULT,
  output [15:0] IO_DATA_OUT
);

  wire BYPASS_CORE, COUNTER_NOT_ZERO, input_parser_1_is_inf, input_parser_1_is_nan, input_parser_1_is_zero,
       input_parser_1_sign, IS_DENORM, not_1_out, or_2_out, RESULT_FOR_SQRT, SECOND_OR_MORE_TACT,
       special_case_handler_1_is_nan, special_case_handler_1_is_ninf, special_case_handler_1_is_pinf;
  wire [4:0] EXP, EXP_RES;
  wire [7:0] COUNTER, not_2_out;
  wire [9:0] MANT;
  wire [10:0] MANT_SQRT;
  wire [15:0] ANSWER, assemble_answer_1_answer, get_exp_mant_1_norm_mant, memory_16bits_1_val, SPECIAL_OUT;

  // Probe on ANSWER
  not not_1 (not_1_out, SECOND_OR_MORE_TACT);
  Transistor #(.width(16)) transistor_1 (.in(ANSWER), .out(IO_DATA_IN), .gate(not_1_out));
  Transistor #(.\type ("n"), .width(16)) transistor_2 (.in(ANSWER), .out(IO_DATA_IN), .gate(SECOND_OR_MORE_TACT));
  // Probe on MANT
  // Probe on EXP
  // Probe on COUNTER
  clk_counter clk_counter_1 (.CLK(CLK), .ENABLE(ENABLE), .VAL(COUNTER));
  // Probe on memory_16bits_1_val
  memory_16bits memory_16bits_1 (.DATA(IO_DATA_IN), .C(COUNTER_NOT_ZERO), .ENABLE(ENABLE), .VAL(memory_16bits_1_val));
  // Probe on MANT_SQRT
  // Probe on get_exp_mant_1_norm_mant
  get_exp_mant get_exp_mant_1 (
    .MANT(MANT), .EXP(EXP), .IS_DENORM(IS_DENORM), .NORM_MANT(get_exp_mant_1_norm_mant), .EXP_RES(EXP_RES));
  // Probe on EXP_RES
  // Probe on EXP_RES
  input_parser input_parser_1 (
    .N(memory_16bits_1_val), .Mant(MANT), .Exp(EXP), .Sign(input_parser_1_sign),
    .IS_ZERO(input_parser_1_is_zero), .IS_DENORM(IS_DENORM), .IS_NAN(input_parser_1_is_nan),
    .IS_INF(input_parser_1_is_inf));
  or or_1 (COUNTER_NOT_ZERO, COUNTER[0], COUNTER[1], COUNTER[2], COUNTER[3], COUNTER[4], COUNTER[5], COUNTER[6], COUNTER[7]);
  assign not_2_out = ~8'h2;  // NOT_Gate not_2, 8 bits wide
  assemble_answer assemble_answer_1 (.MANT_SQRT(MANT_SQRT), .ODD_EXP(EXP_RES), .ANSWER(assemble_answer_1_answer));
  special_case_handler special_case_handler_1 (
    .N(memory_16bits_1_val), .Sign(input_parser_1_sign), .IS_ZERO_INP(input_parser_1_is_zero),
    .IS_NAN_INP(input_parser_1_is_nan), .IS_INF_INP(input_parser_1_is_inf), .SPECIAL_OUT(SPECIAL_OUT),
    .IS_PINF(special_case_handler_1_is_pinf), .IS_NAN(special_case_handler_1_is_nan),
    .IS_NINF(special_case_handler_1_is_ninf), .BYPASS_CORE(BYPASS_CORE));
  sum8 sum8_1 (.A(COUNTER), .B(not_2_out), .Cin(1'b1), .Cout(SECOND_OR_MORE_TACT));  // open: S
  // Probe on SPECIAL_OUT
  calc_sqrt calc_sqrt_1 (
    .MANT(get_exp_mant_1_norm_mant), .COUNTER(COUNTER), .CLK(CLK), .ENABLE(ENABLE), .RESULT(RESULT_FOR_SQRT),
    .MANT_SQRT(MANT_SQRT));
  // Probe on MANT_SQRT
  // Probe on ANSWER
  mux_2to1_16bit mux_2to1_16bit_1 (.D1(SPECIAL_OUT), .D0(assemble_answer_1_answer), .COND(BYPASS_CORE), .RES(ANSWER));
  or or_2 (or_2_out, BYPASS_CORE, RESULT_FOR_SQRT);
  and and_1 (IS_NAN, SECOND_OR_MORE_TACT, special_case_handler_1_is_nan);
  and and_2 (IS_PINF, SECOND_OR_MORE_TACT, special_case_handler_1_is_pinf);
  and and_3 (IS_NINF, SECOND_OR_MORE_TACT, special_case_handler_1_is_ninf);
  and and_4 (RESULT, SECOND_OR_MORE_TACT, or_2_out);

  assign IO_DATA_OUT = IO_DATA_IN;

  // Other names for the same wires on the sheet: CLK2 = CLK; DATA_IN[15:0] = IO_DATA_IN; ENABLE2 = ENABLE;
  //   ENABLE3 = ENABLE; SECOND_OR_MORE_TACT2 = SECOND_OR_MORE_TACT
endmodule

module sum1 (
  input  A,
  input  B,
  input  Cin,
  output S,
  output Cout
);

  wire and_1_out, and_2_out, xor_1_out;

  xor xor_1 (xor_1_out, A, B);
  xor xor_2 (S, xor_1_out, Cin);
  and and_1 (and_1_out, xor_1_out, Cin);
  and and_2 (and_2_out, A, B);
  or or_1 (Cout, and_1_out, and_2_out);
endmodule

module sum2 (
  input  [1:0] A,
  input  [1:0] B,
  input  Cin,
  output [1:0] S,
  output Cout
);

  wire sum1_1_cout;

  sum1 sum1_1 (.A(A[0]), .B(B[0]), .Cin(Cin), .S(S[0]), .Cout(sum1_1_cout));
  sum1 sum1_2 (.A(A[1]), .B(B[1]), .Cin(sum1_1_cout), .S(S[1]), .Cout(Cout));
endmodule

module sum4 (
  input  [3:0] A,
  input  [3:0] B,
  input  Cin,
  output [3:0] S,
  output Cout
);

  wire sum2_1_cout;

  sum2 sum2_1 (.A(A[1:0]), .B(B[1:0]), .Cin(Cin), .S(S[1:0]), .Cout(sum2_1_cout));
  sum2 sum2_2 (.A(A[3:2]), .B(B[3:2]), .Cin(sum2_1_cout), .S(S[3:2]), .Cout(Cout));

  // Other names for the same wires on the sheet: A1[1:0] = A[3:2]; B1[1:0] = B[3:2]
endmodule

module sum8 (
  input  [7:0] A,
  input  [7:0] B,
  input  Cin,
  output [7:0] S,
  output Cout
);

  wire sum4_1_cout;

  sum4 sum4_1 (.A(A[3:0]), .B(B[3:0]), .Cin(Cin), .S(S[3:0]), .Cout(sum4_1_cout));
  sum4 sum4_2 (.A(A[7:4]), .B(B[7:4]), .Cin(sum4_1_cout), .S(S[7:4]), .Cout(Cout));

  // Other names for the same wires on the sheet: A1[3:0] = A[7:4]; B1[3:0] = B[7:4]
endmodule

module sum16 (
  input  [15:0] A,
  input  [15:0] B,
  input  Cin,
  output [15:0] S,
  output Cout
);

  wire sum8_1_cout;

  sum8 sum8_1 (.A(A[7:0]), .B(B[7:0]), .Cin(Cin), .S(S[7:0]), .Cout(sum8_1_cout));
  sum8 sum8_2 (.A(A[15:8]), .B(B[15:8]), .Cin(sum8_1_cout), .S(S[15:8]), .Cout(Cout));

  // Other names for the same wires on the sheet: A1[7:0] = A[15:8]; B1[7:0] = B[15:8]
endmodule

module sum32 (
  input  [31:0] A,
  input  [31:0] B,
  input  Cin,
  output [31:0] S,
  output Cout
);

  wire sum16_1_cout;

  sum16 sum16_1 (.A(A[15:0]), .B(B[15:0]), .Cin(Cin), .S(S[15:0]), .Cout(sum16_1_cout));
  sum16 sum16_2 (.A(A[31:16]), .B(B[31:16]), .Cin(sum16_1_cout), .S(S[31:16]), .Cout(Cout));

  // Other names for the same wires on the sheet: A1[15:0] = A[31:16]; B1[15:0] = B[31:16]
endmodule

module input_parser (
  input  [15:0] N,
  output [9:0] Mant,
  output [4:0] Exp,
  output Sign,
  output IS_ZERO,
  output IS_DENORM,
  output IS_NAN,
  output IS_INF
);

  wire IS_EXP_0, IS_EXP_MAX, M_0, M_NOT_0;

  nor nor_1 (M_0, N[0], N[1], N[2], N[3], N[4], N[5], N[6], N[7], N[8], N[9]);
  not not_1 (M_NOT_0, M_0);
  nor nor_2 (IS_EXP_0, N[10], N[11], N[12], N[13], N[14]);
  and and_1 (IS_EXP_MAX, N[10], N[11], N[12], N[13], N[14]);
  // Probe on IS_EXP_0
  // Probe on IS_EXP_MAX
  and and_2 (IS_ZERO, IS_EXP_0, M_0);
  and and_3 (IS_DENORM, IS_EXP_0, M_NOT_0);
  and and_4 (IS_NAN, M_NOT_0, IS_EXP_MAX);
  and and_5 (IS_INF, M_0, IS_EXP_MAX);

  assign Exp = N[14:10];
  assign Mant = N[9:0];
  assign Sign = N[15];
endmodule

module special_case_handler (
  input  [15:0] N,
  input  Sign,
  input  IS_ZERO_INP,
  input  IS_NAN_INP,
  input  IS_INF_INP,
  output [15:0] SPECIAL_OUT,
  output IS_PINF,
  output IS_NAN,
  output IS_NINF,
  output BYPASS_CORE
);

  wire and_1_out, and_2_out, and_3_out, and_4_out, not_1_out, not_2_out, not_3_out, not_4_out, not_5_out,
       or_2_out;
  wire [15:0] mux_2to1_16bit_1_res, mux_2to1_16bit_2_res, or_1_out;

  assign or_1_out = N | 16'h7e00;  // OR_Gate or_1, 16 bits wide
  not not_1 (not_1_out, IS_ZERO_INP);
  not not_2 (not_2_out, IS_NAN_INP);
  not not_3 (not_3_out, Sign);
  and and_1 (and_1_out, not_3_out, IS_INF_INP);
  and and_2 (and_2_out, not_2_out, not_1_out, Sign);
  or or_2 (or_2_out, IS_ZERO_INP, and_1_out);
  // Probe on mux_2to1_16bit_1_res
  mux_2to1_16bit mux_2to1_16bit_1 (.D1(or_1_out), .COND(IS_NAN_INP), .RES(mux_2to1_16bit_1_res));  // open: D0
  not not_4 (not_4_out, IS_ZERO_INP);
  // Probe on mux_2to1_16bit_2_res
  mux_2to1_16bit mux_2to1_16bit_2 (
    .D1(16'hfe00), .D0(mux_2to1_16bit_1_res), .COND(and_2_out), .RES(mux_2to1_16bit_2_res));
  not not_5 (not_5_out, Sign);
  and and_3 (and_3_out, Sign, not_4_out);
  and and_4 (and_4_out, Sign, IS_INF_INP);
  and and_5 (IS_PINF, not_5_out, IS_INF_INP);
  or or_3 (IS_NAN, and_3_out, and_4_out, IS_NAN_INP);
  mux_2to1_16bit mux_2to1_16bit_3 (.D1(N), .D0(mux_2to1_16bit_2_res), .COND(or_2_out), .RES(SPECIAL_OUT));
  or or_4 (BYPASS_CORE, IS_PINF, IS_NAN, IS_ZERO_INP);

  assign IS_NINF = 1'b0;
endmodule

module mux_2to1_16bit (
  input  [15:0] D1,
  input  [15:0] D0,
  input  COND,
  output [15:0] RES
);

  wire not_1_out, not_2_out;

  not not_1 (not_1_out, COND);
  not not_2 (not_2_out, COND);
  Transistor #(.width(16)) transistor_1 (.in(D1), .out(RES), .gate(not_1_out));
  Transistor #(.\type ("n"), .width(16)) transistor_2 (.in(D1), .out(RES), .gate(COND));
  Transistor #(.width(16)) transistor_3 (.in(D0), .out(RES), .gate(COND));
  Transistor #(.\type ("n"), .width(16)) transistor_4 (.in(D0), .out(RES), .gate(not_2_out));
endmodule

module rs_trigger_sync (
  input  R,
  input  C,
  input  S,
  input  ENABLE,
  output Q,
  output NOT_Q
);

  wire and_1_out, and_2_out, and_3_out, and_4_out, and_5_out, not_1_out, not_2_out, or_1_out, or_2_out;

  and and_1 (and_1_out, R, C);
  and and_2 (and_2_out, C, S);
  not not_1 (not_1_out, ENABLE);
  not not_2 (not_2_out, ENABLE);
  or or_1 (or_1_out, and_1_out, not_1_out);
  or or_2 (or_2_out, C, not_2_out);
  and and_3 (and_3_out, and_2_out, ENABLE);
  and and_4 (and_4_out, or_1_out, or_2_out);
  and and_5 (and_5_out, or_2_out, and_3_out);
  nor nor_1 (Q, and_4_out, NOT_Q);
  nor nor_2 (NOT_Q, Q, and_5_out);
endmodule

module d_trigger (
  input  D,
  input  C,
  input  ENABLE,
  output Q,
  output NOT_Q
);

  wire not_1_out;

  not not_1 (not_1_out, D);
  rs_trigger_sync rs_trigger_sync_1 (.R(not_1_out), .C(C), .S(D), .ENABLE(ENABLE), .Q(Q), .NOT_Q(NOT_Q));
endmodule

module d_trigger_front (
  input  D,
  input  C,
  input  ENABLE,
  output Q,
  output NOT_Q
);

  wire d_trigger_1_q, not_1_out;

  not not_1 (not_1_out, C);
  d_trigger d_trigger_1 (.D(D), .C(not_1_out), .ENABLE(ENABLE), .Q(d_trigger_1_q));  // open: NOT_Q
  d_trigger d_trigger_2 (.D(d_trigger_1_q), .C(C), .ENABLE(ENABLE), .Q(Q), .NOT_Q(NOT_Q));
endmodule

module memory_2bits (
  input  [1:0] DATA,
  input  C,
  input  ENABLE,
  output [1:0] VAL
);

  d_trigger_front d_trigger_front_1 (.D(DATA[0]), .C(C), .ENABLE(ENABLE), .Q(VAL[0]));  // open: NOT_Q
  d_trigger_front d_trigger_front_2 (.D(DATA[1]), .C(C), .ENABLE(ENABLE), .Q(VAL[1]));  // open: NOT_Q
endmodule

module memory_4bits (
  input  [3:0] DATA,
  input  C,
  input  ENABLE,
  output [3:0] VAL
);

  memory_2bits memory_2bits_1 (.DATA(DATA[1:0]), .C(C), .ENABLE(ENABLE), .VAL(VAL[1:0]));
  memory_2bits memory_2bits_2 (.DATA(DATA[3:2]), .C(C), .ENABLE(ENABLE), .VAL(VAL[3:2]));
endmodule

module memory_8bits (
  input  [7:0] DATA,
  input  C,
  input  ENABLE,
  output [7:0] VAL
);

  memory_4bits memory_4bits_1 (.DATA(DATA[3:0]), .C(C), .ENABLE(ENABLE), .VAL(VAL[3:0]));
  memory_4bits memory_4bits_2 (.DATA(DATA[7:4]), .C(C), .ENABLE(ENABLE), .VAL(VAL[7:4]));
endmodule

module memory_16bits (
  input  [15:0] DATA,
  input  C,
  input  ENABLE,
  output [15:0] VAL
);

  memory_8bits memory_8bits_1 (.DATA(DATA[7:0]), .C(C), .ENABLE(ENABLE), .VAL(VAL[7:0]));
  memory_8bits memory_8bits_2 (.DATA(DATA[15:8]), .C(C), .ENABLE(ENABLE), .VAL(VAL[15:8]));
endmodule

module memory_32bits (
  input  [31:0] DATA,
  input  C,
  input  ENABLE,
  output [31:0] VAL
);

  memory_16bits memory_16bits_1 (.DATA(DATA[15:0]), .C(C), .ENABLE(ENABLE), .VAL(VAL[15:0]));
  memory_16bits memory_16bits_2 (.DATA(DATA[31:16]), .C(C), .ENABLE(ENABLE), .VAL(VAL[31:16]));
endmodule

module clk_counter (
  input  CLK,
  input  ENABLE,
  output [7:0] VAL
);

  wire [7:0] sum8_1_s;

  // Probe on VAL
  memory_8bits memory_8bits_1 (.DATA(sum8_1_s), .C(CLK), .ENABLE(ENABLE), .VAL(VAL));
  sum8 sum8_1 (.A(VAL), .B(8'h1), .S(sum8_1_s));  // open: Cin, Cout
  // Probe on sum8_1_s
endmodule

module mem_2bits_level (
  input  [1:0] DATA,
  input  C,
  input  ENABLE,
  output [1:0] VAL
);

  d_trigger d_trigger_1 (.D(DATA[0]), .C(C), .ENABLE(ENABLE), .Q(VAL[0]));  // open: NOT_Q
  d_trigger d_trigger_2 (.D(DATA[1]), .C(C), .ENABLE(ENABLE), .Q(VAL[1]));  // open: NOT_Q
endmodule

module mem_4bits_level (
  input  [3:0] DATA,
  input  C,
  input  ENABLE,
  output [3:0] VAL
);

  mem_2bits_level mem_2bits_level_1 (.DATA(DATA[1:0]), .C(C), .ENABLE(ENABLE), .VAL(VAL[1:0]));
  mem_2bits_level mem_2bits_level_2 (.DATA(DATA[3:2]), .C(C), .ENABLE(ENABLE), .VAL(VAL[3:2]));
endmodule

module mem_8bits_level (
  input  [7:0] DATA,
  input  C,
  input  ENABLE,
  output [7:0] VAL
);

  mem_4bits_level mem_4bits_level_1 (.DATA(DATA[3:0]), .C(C), .ENABLE(ENABLE), .VAL(VAL[3:0]));
  mem_4bits_level mem_4bits_level_2 (.DATA(DATA[7:4]), .C(C), .ENABLE(ENABLE), .VAL(VAL[7:4]));
endmodule

module mem_16bits_level (
  input  [15:0] DATA,
  input  C,
  input  ENABLE,
  output [15:0] VAL
);

  mem_8bits_level mem_8bits_level_1 (.DATA(DATA[7:0]), .C(C), .ENABLE(ENABLE), .VAL(VAL[7:0]));
  mem_8bits_level mem_8bits_level_2 (.DATA(DATA[15:8]), .C(C), .ENABLE(ENABLE), .VAL(VAL[15:8]));
endmodule

module mux_2to1_32bit (
  input  [31:0] D1,
  input  [31:0] D0,
  input  COND,
  output [31:0] RES
);

  wire not_1_out, not_2_out;

  not not_1 (not_1_out, COND);
  not not_2 (not_2_out, COND);
  Transistor #(.width(32)) transistor_1 (.in(D1), .out(RES), .gate(not_1_out));
  Transistor #(.\type ("n"), .width(32)) transistor_2 (.in(D1), .out(RES), .gate(COND));
  Transistor #(.width(32)) transistor_3 (.in(D0), .out(RES), .gate(COND));
  Transistor #(.\type ("n"), .width(32)) transistor_4 (.in(D0), .out(RES), .gate(not_2_out));
endmodule

module left_shift_32bits (
  input  [31:0] VAL,
  input  [4:0] SHIFT,
  output [31:0] RES
);

  wire [0:0] undriven;
  wire [1:0] undriven_2;
  wire [3:0] undriven_3;
  wire [7:0] undriven_4;
  wire [15:0] undriven_5;
  wire [31:0] mux_2to1_32bit_1_res, mux_2to1_32bit_2_res, mux_2to1_32bit_3_res, mux_2to1_32bit_4_res;

  // Probe on mux_2to1_32bit_1_res
  mux_2to1_32bit mux_2to1_32bit_1 (
    .D1({VAL[30:0], undriven[0]}), .D0(VAL), .COND(SHIFT[0]), .RES(mux_2to1_32bit_1_res));
  // Probe on mux_2to1_32bit_2_res
  mux_2to1_32bit mux_2to1_32bit_2 (
    .D1({mux_2to1_32bit_1_res[29:0], undriven_2}), .D0(mux_2to1_32bit_1_res), .COND(SHIFT[1]),
    .RES(mux_2to1_32bit_2_res));
  // Probe on mux_2to1_32bit_3_res
  mux_2to1_32bit mux_2to1_32bit_3 (
    .D1({mux_2to1_32bit_2_res[27:0], undriven_3}), .D0(mux_2to1_32bit_2_res), .COND(SHIFT[2]),
    .RES(mux_2to1_32bit_3_res));
  // Probe on mux_2to1_32bit_4_res
  mux_2to1_32bit mux_2to1_32bit_4 (
    .D1({mux_2to1_32bit_3_res[23:0], undriven_4}), .D0(mux_2to1_32bit_3_res), .COND(SHIFT[3]),
    .RES(mux_2to1_32bit_4_res));
  // Probe on RES
  mux_2to1_32bit mux_2to1_32bit_5 (
    .D1({mux_2to1_32bit_4_res[15:0], undriven_5}), .D0(mux_2to1_32bit_4_res), .COND(SHIFT[4]), .RES(RES));
endmodule

module calc_sqrt (
  input  [15:0] MANT,
  input  [7:0] COUNTER,
  input  CLK,
  input  ENABLE,
  output RESULT,
  output [10:0] MANT_SQRT
);

  wire CLK2, not_1_out, not_2_out, not_3_out, not_6_out, or_1_out;
  wire [0:0] UPDATED_ANSWER;
  wire [7:0] not_4_out, S_22_MINUS_CNTR_MUL_2_s;
  wire [15:0] undriven;
  wire [15:11] ANSWER;
  wire [31:0] left_shift_32bits_1_res, left_shift_32bits_2_res, mux_2to1_32bit_1_res, not_5_out, sum32_1_s,
       UPDATED_VALUE, VALUE;

  not not_1 (not_1_out, COUNTER[1]);
  or or_1 (or_1_out, COUNTER[0], not_1_out, COUNTER[2], COUNTER[3], COUNTER[5], COUNTER[6], COUNTER[7], COUNTER[4]);
  // Probe on left_shift_32bits_1_res
  left_shift_32bits left_shift_32bits_1 (.VAL({undriven, MANT}), .SHIFT(5'b01010), .RES(left_shift_32bits_1_res));
  // Probe on not_2_out
  not not_2 (not_2_out, or_1_out);
  not not_3 (not_3_out, MANT_SQRT[10]);
  // Probe on {ANSWER[14:11], MANT_SQRT, UPDATED_ANSWER[0]}
  and and_1 (CLK2, CLK, not_3_out);
  // Probe on MANT_SQRT[10]
  // Probe on {ANSWER, MANT_SQRT}
  memory_16bits STORING_ANSWER (
    .DATA({ANSWER[14:11], MANT_SQRT, UPDATED_ANSWER[0]}), .C(CLK2), .ENABLE(ENABLE), .VAL({ANSWER, MANT_SQRT}));
  // Probe on {COUNTER[6:0], 1'b0}
  // Probe on mux_2to1_32bit_1_res
  mux_2to1_32bit mux_2to1_32bit_1 (
    .D1(left_shift_32bits_1_res), .D0(UPDATED_VALUE), .COND(not_2_out), .RES(mux_2to1_32bit_1_res));
  assign not_4_out = ~{COUNTER[6:0], 1'b0};  // NOT_Gate not_4, 8 bits wide
  // Probe on S_22_MINUS_CNTR_MUL_2_s
  sum8 S_22_MINUS_CNTR_MUL_2 (.A(8'h1a), .B(not_4_out), .Cin(1'b1), .S(S_22_MINUS_CNTR_MUL_2_s));  // open: Cout
  // Probe on VALUE
  memory_32bits STORING_MANT (.DATA(mux_2to1_32bit_1_res), .C(CLK2), .ENABLE(ENABLE), .VAL(VALUE));
  // Probe on {ANSWER[13:11], MANT_SQRT, 2'b01}
  left_shift_32bits left_shift_32bits_2 (
    .VAL({{16{1'b0}}, ANSWER[13:11], MANT_SQRT, 2'b01}), .SHIFT(S_22_MINUS_CNTR_MUL_2_s[4:0]),
    .RES(left_shift_32bits_2_res));
  // Probe on left_shift_32bits_2_res
  // Probe on VALUE
  assign not_5_out = ~left_shift_32bits_2_res;  // NOT_Gate not_5, 32 bits wide
  sum32 sum32_1 (.A(VALUE), .B(not_5_out), .Cin(1'b1), .S(sum32_1_s), .Cout(UPDATED_ANSWER[0]));
  // Probe on UPDATED_ANSWER[0]
  not not_6 (not_6_out, UPDATED_ANSWER[0]);
  // Probe on UPDATED_VALUE
  mux_2to1_32bit mux_2to1_32bit_2 (.D1(VALUE), .D0(sum32_1_s), .COND(not_6_out), .RES(UPDATED_VALUE));

  assign RESULT = MANT_SQRT[10];

  // Other names for the same wires on the sheet: CLK_t = CLK2; ENABLE2 = ENABLE; ANSWER[10:0] = MANT_SQRT;
  //   UPDATED_ANSWER[15:1] = {ANSWER[14:11], MANT_SQRT}
endmodule

module assemble_answer (
  input  [10:0] MANT_SQRT,
  input  [4:0] ODD_EXP,
  output [15:0] ANSWER
);


  assign ANSWER = {1'b0, ODD_EXP, MANT_SQRT[9:0]};
endmodule

module highest_bit_2bits (
  input  [1:0] N,
  output [15:0] PLACE
);


  assign PLACE = {{15{1'b0}}, N[1]};
endmodule

module highest_bit_4bits (
  input  [3:0] N,
  output [15:0] PLACE
);

  wire nor_1_out;
  wire [15:0] highest_bit_2bits_1_place, highest_bit_2bits_2_place, sum16_1_s;

  highest_bit_2bits highest_bit_2bits_1 (.N(N[1:0]), .PLACE(highest_bit_2bits_1_place));
  highest_bit_2bits highest_bit_2bits_2 (.N(N[3:2]), .PLACE(highest_bit_2bits_2_place));
  nor nor_1 (nor_1_out, N[2], N[3]);
  sum16 sum16_1 (.A(highest_bit_2bits_2_place), .B(16'h2), .S(sum16_1_s));  // open: Cin, Cout
  mux_2to1_16bit mux_2to1_16bit_1 (.D1(highest_bit_2bits_1_place), .D0(sum16_1_s), .COND(nor_1_out), .RES(PLACE));
endmodule

module highest_bit_8bits (
  input  [7:0] N,
  output [15:0] PLACE
);

  wire nor_1_out;
  wire [15:0] highest_bit_4bits_1_place, highest_bit_4bits_2_place, sum16_1_s;

  highest_bit_4bits highest_bit_4bits_1 (.N(N[3:0]), .PLACE(highest_bit_4bits_1_place));
  highest_bit_4bits highest_bit_4bits_2 (.N(N[7:4]), .PLACE(highest_bit_4bits_2_place));
  nor nor_1 (nor_1_out, N[5], N[4], N[6], N[7]);
  sum16 sum16_1 (.A(highest_bit_4bits_2_place), .B(16'h4), .S(sum16_1_s));  // open: Cin, Cout
  mux_2to1_16bit mux_2to1_16bit_1 (.D1(highest_bit_4bits_1_place), .D0(sum16_1_s), .COND(nor_1_out), .RES(PLACE));
endmodule

module highest_bit_16bits (
  input  [15:0] N,
  output [15:0] PLACE
);

  wire nor_1_out;
  wire [15:0] highest_bit_8bits_1_place, highest_bit_8bits_2_place, sum16_1_s;

  highest_bit_8bits highest_bit_8bits_1 (.N(N[7:0]), .PLACE(highest_bit_8bits_1_place));
  highest_bit_8bits highest_bit_8bits_2 (.N(N[15:8]), .PLACE(highest_bit_8bits_2_place));
  nor nor_1 (nor_1_out, N[11], N[8], N[9], N[10], N[12], N[13], N[14], N[15]);
  sum16 sum16_1 (.A(highest_bit_8bits_2_place), .B(16'h8), .S(sum16_1_s));  // open: Cin, Cout
  mux_2to1_16bit mux_2to1_16bit_1 (.D1(highest_bit_8bits_1_place), .D0(sum16_1_s), .COND(nor_1_out), .RES(PLACE));
endmodule

module get_exp_mant_denorm (
  input  [9:0] MANT,
  output [15:0] NEW_MANT,
  output [4:0] EXP_RES
);

  wire IS_DENORM, IS_EXP_ODD;
  wire [15:0] highest_bit_16bits_1_place, MANT_SHIFT, mux_2to1_16bit_1_res, not_1_out, not_3_out, sum16_1_s;
  wire [15:5] sum16_3_s;
  wire [15:10] undriven;
  wire [31:0] left_shift_32bits_1_res;
  wire [31:10] undriven_2;

  // Probe on highest_bit_16bits_1_place
  highest_bit_16bits highest_bit_16bits_1 (.N({undriven, MANT}), .PLACE(highest_bit_16bits_1_place));
  assign not_1_out = ~highest_bit_16bits_1_place;  // NOT_Gate not_1, 16 bits wide
  not not_2 (IS_EXP_ODD, MANT_SHIFT[0]);
  sum16 sum16_1 (.A({1'b0, MANT_SHIFT[15:1]}), .Cin(MANT_SHIFT[0]), .S(sum16_1_s));  // open: B, Cout
  sum16 sum16_2 (.A(16'ha), .B(not_1_out), .Cin(1'b1), .S(MANT_SHIFT));  // open: Cout
  // Probe on sum16_1_s
  assign not_3_out = ~sum16_1_s;  // NOT_Gate not_3, 16 bits wide
  left_shift_32bits left_shift_32bits_1 (
    .VAL({undriven_2, MANT}), .SHIFT(MANT_SHIFT[4:0]), .RES(left_shift_32bits_1_res));
  sum16 sum16_3 (.A(16'h8), .B(not_3_out), .Cin(1'b1), .S({sum16_3_s, EXP_RES}));  // open: Cout
  // Probe on left_shift_32bits_1_res[15:0]
  // Probe on {sum16_3_s, EXP_RES}
  // Probe on mux_2to1_16bit_1_res
  mux_2to1_16bit mux_2to1_16bit_1 (
    .D1({6'b000001, MANT}), .D0(left_shift_32bits_1_res[15:0]), .COND(IS_DENORM), .RES(mux_2to1_16bit_1_res));
  // Probe on NEW_MANT
  mux_2to1_16bit mux_2to1_16bit_2 (
    .D1(mux_2to1_16bit_1_res), .D0({mux_2to1_16bit_1_res[14:0], 1'b0}), .COND(IS_EXP_ODD), .RES(NEW_MANT));

  // Other names for the same wires on the sheet: MANT2[9:0] = MANT
endmodule

module get_exp_mant_norm (
  input  [9:0] MANT,
  input  [4:0] EXP,
  output [15:0] NEW_MANT,
  output [4:0] EXP_RES
);

  wire [7:0] sum8_1_s;
  wire [7:5] undriven;
  wire [15:0] mux_2to1_16bit_2_res, sum16_1_s;
  wire [15:5] undriven_2;
  wire [15:8] undriven_3;

  // Probe on EXP[0]
  // Probe on {undriven_2, EXP}
  // Probe on sum8_1_s
  sum8 sum8_1 (.A({undriven, EXP}), .B({8{1'b1}}), .S(sum8_1_s));  // open: Cin, Cout
  // Probe on {undriven_3, sum8_1_s}
  // Probe on NEW_MANT
  mux_2to1_16bit mux_2to1_16bit_1 (.D1({6'b000001, MANT}), .D0({5'b00001, MANT, 1'b0}), .COND(EXP[0]), .RES(NEW_MANT));
  // Probe on mux_2to1_16bit_2_res
  mux_2to1_16bit mux_2to1_16bit_2 (
    .D1({undriven_2, EXP}), .D0({undriven_3, sum8_1_s}), .COND(EXP[0]), .RES(mux_2to1_16bit_2_res));
  sum16 sum16_1 (
    .A(16'h10), .B(mux_2to1_16bit_2_res), .S({sum16_1_s[15:6], EXP_RES, sum16_1_s[0]}));  // open: Cin, Cout
endmodule

module get_exp_mant (
  input  [9:0] MANT,
  input  [4:0] EXP,
  input  IS_DENORM,
  output [15:0] NORM_MANT,
  output [4:0] EXP_RES
);

  wire [4:0] get_exp_mant_denorm_1_exp_res, get_exp_mant_norm_1_exp_res;
  wire [15:0] get_exp_mant_denorm_1_new_mant, get_exp_mant_norm_1_new_mant;
  wire [15:5] mux_2to1_16bit_2_res, undriven, undriven_2;

  get_exp_mant_denorm get_exp_mant_denorm_1 (
    .MANT(MANT), .NEW_MANT(get_exp_mant_denorm_1_new_mant), .EXP_RES(get_exp_mant_denorm_1_exp_res));
  get_exp_mant_norm get_exp_mant_norm_1 (
    .MANT(MANT), .EXP(EXP), .NEW_MANT(get_exp_mant_norm_1_new_mant), .EXP_RES(get_exp_mant_norm_1_exp_res));
  // Probe on NORM_MANT
  mux_2to1_16bit mux_2to1_16bit_1 (
    .D1(get_exp_mant_denorm_1_new_mant), .D0(get_exp_mant_norm_1_new_mant), .COND(IS_DENORM), .RES(NORM_MANT));
  mux_2to1_16bit mux_2to1_16bit_2 (
    .D1({undriven, get_exp_mant_denorm_1_exp_res}), .D0({undriven_2, get_exp_mant_norm_1_exp_res}),
    .COND(IS_DENORM), .RES({mux_2to1_16bit_2_res, EXP_RES}));

  // Other names for the same wires on the sheet: IS_DENORM2 = IS_DENORM
endmodule
